// Digital circuit hazard-unit.dig as structural Verilog
module hazard_unit (
  input  [4:0] RR0_2,
  input  [4:0] WR_3,
  input  [4:0] RR1_2,
  input  [4:0] WR_4,
  input  RFW_3,
  input  RFW_4,
  input  MLD_3,
  input  MST_3,
  input  PCbr_2,
  output [1:0] HZRD_RD0sl,
  output [1:0] HZRD_RD1sl,
  output STL_IF,
  output STL_DR,
  output STL_EX,
  output FLS_EX,
  output FLS_IF,
  output FLS_DR
);

  wire and_2_out, and_3_out, and_4_out, and_5_out, comparator_1_eq, comparator_2_eq, comparator_3_eq,
       comparator_4_eq;

  and and_1 (FLS_EX, MLD_3, ~MST_3);  // And
  Comparator #(.Bits(5)) comparator_1 (.a(RR0_2), .b(WR_3), .eq(comparator_1_eq));  // open: gt, lt
  Comparator #(.Bits(5)) comparator_2 (.a(RR0_2), .b(WR_4), .eq(comparator_2_eq));  // open: gt, lt
  Comparator #(.Bits(5)) comparator_3 (.a(RR1_2), .b(WR_3), .eq(comparator_3_eq));  // open: gt, lt
  Comparator #(.Bits(5)) comparator_4 (.a(RR1_2), .b(WR_4), .eq(comparator_4_eq));  // open: gt, lt
  and and_2 (and_2_out, comparator_3_eq, RFW_3);
  and and_3 (and_3_out, comparator_4_eq, RFW_4);
  and and_4 (and_4_out, comparator_1_eq, RFW_3);
  and and_5 (and_5_out, comparator_2_eq, RFW_4);
  PriorityEncoder #(.Selector_Bits(2)) priorityencoder_1 (
    .in0(1'b0), .in1(and_4_out), .in2(and_5_out), .in3(1'b0), .num(HZRD_RD0sl));  // open: any
  PriorityEncoder #(.Selector_Bits(2)) priorityencoder_2 (
    .in0(1'b0), .in1(and_2_out), .in2(and_3_out), .in3(1'b0), .num(HZRD_RD1sl));  // open: any

  assign FLS_DR = PCbr_2;
  assign FLS_IF = PCbr_2;
  assign STL_DR = FLS_EX;
  assign STL_EX = FLS_EX;
  assign STL_IF = FLS_EX;
endmodule
